# Fritzing sketch CIRCUIT (saved by Fritzing 0.9.6b)
breadboards: 1

parts:
  S1 = Round Pushbutton
  GSM_SIM_GPSR_SMS_SIM900_SIM1 = SIM800L [package=THT]
  A1 = NEO-6M GPS Module [part_number=GY-GPS6MV2]
  CPU1 = NodeMCU WROOM ESP 32
  HC-SR04_Sensor_1 = HC-SR04 Ultrasonic Distance Sensor
  Water_Level_Sensor1 = Water Level Sensor
  VCC1 = Battery
  J1 = Piezo Speaker
  U1 = Vibration Motor- ROB-08449 [package=vibe-motor-10mm]

nets:
  N1: S1.leg0, CPU1.pin_11
  GND: S1.leg1, GSM_SIM_GPSR_SMS_SIM900_SIM1.GND, A1.GND, CPU1.pin_18, HC-SR04_Sensor_1.GND, Water_Level_Sensor1.GND, VCC1.-, J1.pin1, U1.+
  N2: GSM_SIM_GPSR_SMS_SIM900_SIM1.SIM_TXD, CPU1.pin_21
  N3: GSM_SIM_GPSR_SMS_SIM900_SIM1.SIM_RXD, CPU1.pin_20
  N4: A1.Tx, CPU1.pin_22
  N5: A1.Rx, CPU1.pin_23
  N6: CPU1.pin_4, CPU1.pin_5, Water_Level_Sensor1.SIG
  N7: CPU1.pin_8, CPU1.pin_9, CPU1.pin_24, CPU1.pin_25, CPU1.pin_26, HC-SR04_Sensor_1.TRIG, HC-SR04_Sensor_1.ECHO, J1.pin2
  N8: CPU1.pin_10, U1.-
  N9: CPU1.pin_15, CPU1.pin_16, HC-SR04_Sensor_1.VCC, VCC1.+
  N10: CPU1.pin_17, Water_Level_Sensor1.VCC

custom parts:
  NEO-6M GPS Module: GY-GPS6MV2 NEO-6M GPS Module Module based on U-blox NEO-6M GPS engine, incorporating regulator for 3.3-5V DC input, MS621FE-compatible rechargeable battery for backup and EEPROM for storing configuration settings. Links: NEO-6 series product information page NEO-6 Datasheet
  NodeMCU WROOM ESP 32: 30 pol Development Kit
  Water Level Sensor: A water level sensor. This sensor operates at 3V to 5V. The Sig (signal) pin outputs an analogue signal that is in proportion to the amount of water in contact with the sensor.
